# Fritzing sketch longboard (saved by Fritzing 0.9.3b)
breadboards: 1

parts:
  Part1 = Arduino Nano (Rev3.0)
  RGB_SMD_LED1 = SMD RGB LED (WS2812) [package=5050]
  S1 = Toggle Switch [package=THT]

nets:
  N1: Part1.GND, S1.L2
  5V: Part1.5V, RGB_SMD_LED1.VCC, S1.COM
