# Fritzing sketch room_lights_v1 (saved by Fritzing 0.9.3b)
breadboards: 1

parts:
  Part1 = Arduino Uno (Rev3)
  RGB_SMD_LED1 = SMD RGB LED (WS2812) [package=5050]
  S1 = Pushbutton [package="[THT]"]
  R1 = Resistor [tolerance=±5% resistance=1k package="0603 [SMD]"]
  U1 = POT [package=pot_mammoth]

nets:
  N1: Part1.A0, U1.A
  N2: Part1.D8, RGB_SMD_LED1.DIn
  N3: Part1.D3_PWM, S1.Pin_1, S1.Pin_2, R1.Pin_0
  5V: Part1.5V, RGB_SMD_LED1.VCC, S1.Pin_3, S1.Pin_4, U1.S
  N4: Part1.GND, RGB_SMD_LED1.DOut, R1.Pin_1, U1.E
